// Logisim project CPU.circ as structural Verilog: 6 circuits, main circuit CPU
module CPU (
  output [15:0] out_1,
  output Type,
  output [3:0] out_3,
  output [3:0] out_4,
  output [3:0] out_5,
  output [3:0] Data_In
);

  wire CLK, count_1_count, reg_write_1_out;
  wire [3:0] Reg_File_a_data;
  wire [4:0] counter_1_q;

  Clock clock_1 (.out(CLK));
  Counter #(.width(5), .max('h1f)) counter_1 (
    .count(count_1_count), .Q(counter_1_q), .clk(CLK));  // open: load, D, carry, clr
  Count count_1 (.X0(out_1[15]), .X1(out_1[14]), .X2(out_1[13]), .X3(out_1[12]), .Count(count_1_count));
  Reg_Write reg_write_1 (.X1(out_1[15]), .X2(out_1[14]), .X3(out_1[13]), .Out(reg_write_1_out));
  ROM #(.addrWidth(5), .dataWidth(16)) rom_1 (.addr(counter_1_q), .data(out_1));  // open: sel
  Type type_1 (.X3(out_1[15]), .X2(out_1[14]), .X1(out_1[13]), .X0(out_1[12]), .Type(Type));
  Reg_File Reg_File (
    .A(out_1[7:4]), .B(out_1[3:0]), .C(out_1[11:8]), .Data_In(Data_In), .Reg_Write(reg_write_1_out),
    .CLK(CLK), .A_DATA(Reg_File_a_data), .B_DATA(out_3));
  // Probe on out_1[15:12]
  // Probe on out_1[11:8]
  // Probe on out_1[7:4]
  Multiplexer #(.width(4), .enable("false")) multiplexer_1 (.in0(out_3), .in1(out_1[3:0]), .out(out_5), .sel(Type));
  // Probe on Data_In
  // Probe on Data_In
  // Probe on out_1[3:0]
  ALU alu_1 (.A(Reg_File_a_data), .B(out_5), .Out(Data_In), .ALU_Ctrl(out_1[15:12]));

  assign out_4 = out_1[3:0];

  // Other names for the same wires on the sheet: B[3:0] = out_1[3:0]; A[3:0] = out_1[7:4]; C[3:0] = out_1[11:8];
  //   OpCode[3:0] = out_1[15:12]

  // Notes on the sheet:
  //   LanQing Cheng   914955364
  //   Chengwei Su   913705052
  //   Count
  //   Instruction
  //   Reg_Write
  //   contents of rom_1 (hex, n*v repeats v):
  //   2003 2106 1005 3210 4301 5433 6520 763c 8720 986f b938 ca77 db13 ec62 fd85 e05
  //   Type = 0 , R-type / Type = 1, I-type
endmodule

module Reg_File (
  input  [3:0] A,
  input  [3:0] B,
  input  [3:0] C,
  input  [3:0] Data_In,
  input  Reg_Write,
  input  CLK,
  output [3:0] A_DATA,
  output [3:0] B_DATA
);

  wire Write_Reg0, Write_Reg1, Write_Reg2, Write_Reg3, Write_Reg4, Write_Reg5, Write_Reg6, Write_Reg7,
       Write_Reg8, Write_Reg9, Write_Reg10, Write_Reg11, Write_Reg12, Write_Reg13, Write_Reg14, Write_Reg15;
  wire [3:0] Reg0, Reg1, Reg2, Reg3, Reg4, Reg5, Reg6, Reg7, Reg8, Reg9, Reg10, Reg11, Reg12, Reg13, Reg14,
       Reg15;

  Demultiplexer #(.select(4), .enable("false")) demultiplexer_1 (
    .out0(Write_Reg0), .out1(Write_Reg1), .out2(Write_Reg2), .out3(Write_Reg3), .out4(Write_Reg4),
    .out5(Write_Reg5), .out6(Write_Reg6), .out7(Write_Reg7), .out8(Write_Reg8), .out9(Write_Reg9),
    .out10(Write_Reg10), .out11(Write_Reg11), .out12(Write_Reg12), .out13(Write_Reg13), .out14(Write_Reg14),
    .out15(Write_Reg15), .in(Reg_Write), .sel(C));
  // Probe on Reg0
  Register #(.width(4)) u_Reg0 (.D(Data_In), .en(Write_Reg0), .Q(Reg0), .clk(CLK));  // open: clr
  // Probe on Reg4
  Register #(.width(4)) u_Reg4 (.D(Data_In), .en(Write_Reg4), .Q(Reg4), .clk(CLK));  // open: clr
  // Probe on Reg8
  Register #(.width(4)) u_Reg8 (.D(Data_In), .en(Write_Reg8), .Q(Reg8), .clk(CLK));  // open: clr
  // Probe on Reg12
  Register #(.width(4)) u_Reg12 (.D(Data_In), .en(Write_Reg12), .Q(Reg12), .clk(CLK));  // open: clr
  // Probe on Reg1
  Register #(.width(4)) u_Reg1 (.D(Data_In), .en(Write_Reg1), .Q(Reg1), .clk(CLK));  // open: clr
  // Probe on Reg5
  Register #(.width(4)) u_Reg5 (.D(Data_In), .en(Write_Reg5), .Q(Reg5), .clk(CLK));  // open: clr
  // Probe on Reg9
  Register #(.width(4)) u_Reg9 (.D(Data_In), .en(Write_Reg9), .Q(Reg9), .clk(CLK));  // open: clr
  // Probe on Reg13
  Register #(.width(4)) u_Reg13 (.D(Data_In), .en(Write_Reg13), .Q(Reg13), .clk(CLK));  // open: clr
  Register #(.width(4)) u_Reg2 (.D(Data_In), .en(Write_Reg2), .Q(Reg2), .clk(CLK));  // open: clr
  Register #(.width(4)) u_Reg6 (.D(Data_In), .en(Write_Reg6), .Q(Reg6), .clk(CLK));  // open: clr
  Register #(.width(4)) u_Reg10 (.D(Data_In), .en(Write_Reg10), .Q(Reg10), .clk(CLK));  // open: clr
  Register #(.width(4)) u_Reg14 (.D(Data_In), .en(Write_Reg14), .Q(Reg14), .clk(CLK));  // open: clr
  // Probe on Reg2
  // Probe on Reg6
  // Probe on Reg10
  // Probe on Reg14
  // Probe on Reg3
  Register #(.width(4)) u_Reg3 (.D(Data_In), .en(Write_Reg3), .Q(Reg3), .clk(CLK));  // open: clr
  // Probe on Reg7
  Register #(.width(4)) u_Reg7 (.D(Data_In), .en(Write_Reg7), .Q(Reg7), .clk(CLK));  // open: clr
  // Probe on Reg11
  Register #(.width(4)) u_Reg11 (.D(Data_In), .en(Write_Reg11), .Q(Reg11), .clk(CLK));  // open: clr
  // Probe on Reg15
  Register #(.width(4)) u_Reg15 (.D(Data_In), .en(Write_Reg15), .Q(Reg15), .clk(CLK));  // open: clr
  Multiplexer #(.select(4), .width(4), .enable("false")) multiplexer_1 (
    .in0(Reg0), .in1(Reg1), .in2(Reg2), .in3(Reg3), .in4(Reg4), .in5(Reg5), .in6(Reg6), .in7(Reg7),
    .in8(Reg8), .in9(Reg9), .in10(Reg10), .in11(Reg11), .in12(Reg12), .in13(Reg13), .in14(Reg14),
    .in15(Reg15), .out(A_DATA), .sel(A));
  Multiplexer #(.select(4), .width(4), .enable("false")) multiplexer_2 (
    .in0(Reg0), .in1(Reg1), .in2(Reg2), .in3(Reg3), .in4(Reg4), .in5(Reg5), .in6(Reg6), .in7(Reg7),
    .in8(Reg8), .in9(Reg9), .in10(Reg10), .in11(Reg11), .in12(Reg12), .in13(Reg13), .in14(Reg14),
    .in15(Reg15), .out(B_DATA), .sel(B));
endmodule

module ALU (
  input  [3:0] A,
  input  [3:0] B,
  input  [3:0] ALU_Ctrl,
  output [3:0] Out
);

  wire [3:0] adder_1_out, and_1_out, negator_1_out, not_1_out, or_1_out, subtractor_1_out, xor_1_out;

  assign and_1_out = A & B;  // AND_Gate and_1, 4 bits wide
  assign or_1_out = A | B;  // OR_Gate or_1, 4 bits wide
  assign xor_1_out = A ^ B;  // XOR_Gate xor_1, 4 bits wide
  assign not_1_out = ~A;  // NOT_Gate not_1, 4 bits wide
  Negator #(.width(4)) negator_1 (.in(A), .out(negator_1_out));
  Adder #(.width(4)) adder_1 (.a(A), .b(B), .out(adder_1_out));  // open: cin, cout
  Subtractor #(.width(4)) subtractor_1 (.a(A), .b(B), .out(subtractor_1_out));  // open: bin, bout
  Multiplexer #(.select(4), .width(4), .enable("false")) multiplexer_1 (
    .in0(4'b0000), .in2(B), .in3(A), .in4(and_1_out), .in5(and_1_out), .in6(or_1_out), .in7(or_1_out),
    .in8(xor_1_out), .in9(xor_1_out), .in10(not_1_out), .in11(negator_1_out), .in12(adder_1_out),
    .in13(adder_1_out), .in14(subtractor_1_out), .in15(subtractor_1_out), .out(Out), .sel(ALU_Ctrl));  // open: in1
endmodule

module Type (
  input  X3,
  input  X2,
  input  X1,
  input  X0,
  output Type
);

  wire and_1_out, and_2_out, and_3_out, not_1_out, not_2_out, not_3_out, not_4_out;

  not not_1 (not_1_out, X3);
  not not_2 (not_2_out, X2);
  and and_1 (and_1_out, not_1_out, not_2_out, not_3_out);
  not not_3 (not_3_out, X0);
  not not_4 (not_4_out, X1);
  and and_2 (and_2_out, not_4_out, X0);
  and and_3 (and_3_out, X2, X0);
  or or_1 (Type, and_1_out, and_2_out, and_3_out);
endmodule

module Reg_Write (
  input  X1,
  input  X2,
  input  X3,
  output Out
);

  or or_1 (Out, X1, X2, X3);
endmodule

module Count (
  input  X0,
  input  X1,
  input  X2,
  input  X3,
  output Count
);

  or or_1 (Count, X0, X1, X2, X3);
endmodule
