// Logisim project 4BitParity.circ as structural Verilog: 5 circuits, main circuit main
module main (
  input  Halt_Enable
);

  wire and_2_out, CLK, Correct, Done_Testing, Halt, Input, not_1_out, not_2_out, not_3_out, Solution,
       YourAnswer;
  wire [6:0] counter_1_q, TestNumber;

  not not_1 (not_1_out, Correct);
  Clock clock_1 (.out(CLK));
  and and_1 (Halt, Halt_Enable, not_1_out);
  Inputs inputs_1 (.Halt(Halt), .CLK(CLK), .Input(Input), .TestNumber(TestNumber), .Done_Testing(Done_Testing));
  _4BitEvenParity u_4bitevenparity_1 (.Input(Input), .CLK(CLK), .Is_Even(YourAnswer));
  // Probe on Input
  // Probe on YourAnswer
  // Probe on Solution
  // Probe on Correct
  not not_2 (not_2_out, Halt);
  and and_2 (and_2_out, Correct, not_2_out, not_3_out);
  not not_3 (not_3_out, Done_Testing);
  Checker checker_1 (.Your_Answer(YourAnswer), .TestNumber(TestNumber), .Correct(Correct), .Solution(Solution));
  Counter #(.width(7), .max('h41), .ongoal("stay")) counter_1 (
    .count(and_2_out), .Q(counter_1_q), .clk(CLK));  // open: load, D, carry, clr
  // Probe on counter_1_q

  // Notes on the sheet:
  //   Chengwei Su
  //   913705052
  //   LanQing Cheng
  //   914955364
  //   Max 65
endmodule

module _4BitEvenParity (
  input  Input,
  input  CLK,
  output Is_Even
);

  wire A, Ap, B, Bp, C, Cp, D, Dp;

  NewTreeGraph newtreegraph_1 (
    .A(A), .B(B), .C(C), .D(D), .in(Input), .Ap(Ap), .Bp(Bp), .Cp(Cp), .Dp(Dp), .out(Is_Even));
  D_Flip_Flop d_ff_1 (.clk(CLK), .D(Ap), .Q(A));  // open: Qn, preset, en, reset
  D_Flip_Flop d_ff_2 (.clk(CLK), .D(Bp), .Q(B));  // open: Qn, preset, en, reset
  D_Flip_Flop d_ff_3 (.clk(CLK), .D(Cp), .Q(C));  // open: Qn, preset, en, reset
  D_Flip_Flop d_ff_4 (.clk(CLK), .D(Dp), .Q(D));  // open: Qn, preset, en, reset

  // Other names for the same wires on the sheet: out = Is_Even
endmodule

module Inputs (
  input  Halt,
  input  CLK,
  output Input,
  output [6:0] TestNumber,
  output Done_Testing
);

  wire not_1_out;

  not not_1 (not_1_out, Halt);
  Counter #(.width(7), .max('h41), .ongoal("stay")) counter_1 (
    .count(not_1_out), .Q(TestNumber), .carry(Done_Testing), .clk(CLK));  // open: load, D, clr
  ROM #(.addrWidth(7), .dataWidth(1)) rom_1 (.addr(TestNumber), .data(Input));  // open: sel

  // Notes on the sheet:
  //   contents of rom_1 (hex, n*v repeats v):
  //   7*0 1 0 0 1 0 0 0 1 1 0 1 0 0 0 1 0 1 0 1 1 0 0 4*1 0 0 0 1 0 0 1 1 0 1 0 1 0 4*1 0 0 1 1 0 4*1 0
  //   4*1
endmodule

module Checker (
  input  Your_Answer,
  input  [6:0] TestNumber,
  output Correct,
  output Solution
);

  ROM #(.addrWidth(7), .dataWidth(1)) rom_1 (.addr(TestNumber), .data(Solution));  // open: sel
  Comparator #(.width(1)) comparator_1 (.a(Solution), .b(Your_Answer), .eq(Correct));  // open: gt, lt

  // Notes on the sheet:
  //   contents of rom_1 (hex, n*v repeats v):
  //   4*0 1 11*0 1 7*0 1 0 0 0 1 11*0 1 0 0 0 1 7*0 1 11*0 1
endmodule

module NewTreeGraph (
  input  A,
  input  B,
  input  C,
  input  D,
  input  in,
  output Ap,
  output Bp,
  output Cp,
  output Dp,
  output out
);

  wire and_1_out, and_2_out, and_3_out, and_4_out, and_5_out, and_6_out, and_7_out, and_8_out, and_9_out,
       and_10_out, and_11_out, and_12_out, and_13_out, and_14_out, and_15_out, and_16_out, and_17_out,
       and_18_out, and_19_out, and_20_out, and_21_out, and_22_out, and_23_out, and_24_out, and_25_out,
       not_1_out, not_2_out, not_3_out, not_4_out, not_5_out, not_6_out, not_7_out, not_8_out, not_9_out,
       not_10_out, not_11_out, not_12_out, not_13_out, not_14_out, not_15_out, not_16_out, not_17_out,
       not_18_out, not_19_out, not_20_out, not_21_out, not_22_out, not_23_out, not_24_out, not_25_out,
       not_26_out, not_27_out, not_28_out, not_29_out, not_30_out, not_31_out, not_32_out, not_33_out,
       not_34_out, not_35_out, not_36_out, not_37_out, not_38_out, not_39_out, not_40_out, not_41_out,
       not_42_out, not_43_out, not_44_out, not_45_out;

  not not_1 (not_1_out, D);
  not not_2 (not_2_out, in);
  not not_3 (not_3_out, C);
  not not_4 (not_4_out, D);
  not not_5 (not_5_out, A);
  not not_6 (not_6_out, C);
  not not_7 (not_7_out, A);
  not not_8 (not_8_out, B);
  not not_9 (not_9_out, C);
  not not_10 (not_10_out, D);
  not not_11 (not_11_out, in);
  not not_12 (not_12_out, A);
  not not_13 (not_13_out, B);
  not not_14 (not_14_out, C);
  not not_15 (not_15_out, D);
  not not_16 (not_16_out, A);
  not not_17 (not_17_out, B);
  not not_18 (not_18_out, in);
  not not_19 (not_19_out, B);
  not not_20 (not_20_out, A);
  not not_21 (not_21_out, D);
  not not_22 (not_22_out, in);
  not not_23 (not_23_out, C);
  not not_24 (not_24_out, D);
  not not_25 (not_25_out, in);
  not not_26 (not_26_out, A);
  not not_27 (not_27_out, B);
  not not_28 (not_28_out, C);
  not not_29 (not_29_out, in);
  not not_30 (not_30_out, A);
  not not_31 (not_31_out, C);
  not not_32 (not_32_out, D);
  not not_33 (not_33_out, in);
  not not_34 (not_34_out, A);
  not not_35 (not_35_out, B);
  not not_36 (not_36_out, C);
  not not_37 (not_37_out, D);
  not not_38 (not_38_out, in);
  not not_39 (not_39_out, C);
  not not_40 (not_40_out, D);
  not not_41 (not_41_out, in);
  not not_42 (not_42_out, in);
  not not_43 (not_43_out, C);
  not not_44 (not_44_out, B);
  not not_45 (not_45_out, D);
  and and_1 (and_1_out, B, not_1_out, in);
  and and_2 (and_2_out, B, D, not_2_out);
  and and_3 (and_3_out, B, C);
  and and_4 (and_4_out, A, not_3_out, not_4_out);
  and and_5 (and_5_out, not_5_out, not_6_out, D, in);
  and and_6 (and_6_out, not_7_out, not_8_out, C);
  and and_7 (and_7_out, B, not_9_out, not_10_out, not_11_out);
  and and_8 (and_8_out, not_12_out, not_13_out, not_14_out, not_15_out, in);
  and and_9 (and_9_out, not_16_out, not_17_out, D, not_18_out);
  and and_10 (and_10_out, not_19_out, C, D);
  and and_11 (and_11_out, not_20_out, B, not_21_out, not_22_out);
  and and_12 (and_12_out, B, D, in);
  and and_13 (and_13_out, A, not_23_out, not_24_out, not_25_out);
  and and_14 (and_14_out, A, D, in);
  and and_15 (and_15_out, A, C, in);
  and and_16 (and_16_out, not_26_out, not_27_out, not_28_out, not_29_out);
  and and_17 (and_17_out, not_30_out, not_31_out, not_32_out, not_33_out);
  and and_18 (and_18_out, not_34_out, not_35_out, C, in);
  and and_19 (and_19_out, B, not_36_out, D, in);
  and and_20 (and_20_out, B, C, not_37_out, in);
  and and_21 (and_21_out, B, C, D, not_38_out);
  and and_22 (and_22_out, A, not_39_out, not_40_out, in);
  and and_23 (and_23_out, A, D, not_41_out);
  and and_24 (and_24_out, A, C, not_42_out);
  and and_25 (and_25_out, A, B, not_43_out);
  and and_26 (out, A, not_44_out, C, not_45_out);
  or or_1 (Ap, and_1_out, and_2_out, and_3_out, and_4_out);
  or or_2 (Bp, and_5_out, and_6_out, and_7_out);
  or or_3 (Cp, and_8_out, and_9_out, and_10_out, and_11_out, and_12_out, and_13_out, and_14_out, and_15_out);
  or or_4 (Dp, and_16_out, and_17_out, and_18_out, and_19_out, and_20_out, and_21_out, and_22_out, and_23_out, and_24_out, and_25_out);
endmodule
